// Logisim project SD_Group05.circ as structural Verilog: 3 circuits, main circuit main
module main (
  output [11:0] pc,
  output [11:0] r0,
  output [11:0] r1,
  output [11:0] r2,
  output [11:0] r3,
  output [11:0] r4,
  output [11:0] r5,
  output [11:0] r6,
  output [11:0] r7,
  output halt
);

  wire and_1_out, clock_1_out, reset_out;
  wire [15:0] undriven;

  Halt halt_1 (.instruction(undriven), .clock(clock_1_out), .reset(reset_out), .halt(halt));
  Clock clock_1 (.out(clock_1_out));
  Button reset (.out(reset_out));
  and and_1 (and_1_out, ~halt, clock_1_out);  // AND_Gate

  // Notes on the sheet:
  //   current instruction
  //   clock signal
  //   reset button
  //   DO NOT CHANGE THE INPUTS AND OUTPUTS OF THIS CIRCUIT! Do not add/remove inputs or outputs. Do not even change their location or orientation.
endmodule

module Halt (
  input  [15:0] instruction,
  input  clock,
  input  reset,
  output halt
);

  wire and_1_out, comparator_1_eq, comparator_2_gt, counter_1_carry, or_1_out, or_2_out;
  wire [11:0] counter_1_q;

  Comparator #(.width(16), .mode("unsigned")) comparator_1 (
    .a(instruction), .b({16{1'b0}}), .eq(comparator_1_eq));  // open: gt, lt
  Counter #(.width(12), .max('hfff), .trigger("falling")) counter_1 (
    .Q(counter_1_q), .carry(counter_1_carry), .clk(clock), .clr(reset));  // open: load, D, count
  or or_1 (or_1_out, comparator_1_eq, counter_1_carry);
  Comparator #(.width(12), .mode("unsigned")) comparator_2 (
    .a(counter_1_q), .b({12{1'b0}}), .gt(comparator_2_gt));  // open: eq, lt
  or or_2 (or_2_out, halt, and_1_out);
  and and_1 (and_1_out, or_1_out, comparator_2_gt);
  Register #(.width(1)) register_1 (.D(or_2_out), .Q(halt), .clk(clock), .clr(reset));  // open: en

  // Notes on the sheet:
  //   halt becomes and stays asserted if the instruction is 0000 (not in the first clock cycle) or the end of the counter is reached (2^12)
endmodule

module PC (
  input  branch_rel,
  input  branch_abs,
  input  [11:0] branch_val,
  input  C,
  input  reset,
  output [11:0] instruction_address
);

  wire nor_1_out;
  wire [11:0] bit_extender_1_out, multiplexer_1_out, multiplexer_2_out, n12_bit_cla_1_som, n12_bit_cla_2_som;

  assign bit_extender_1_out = {{11{1'b0}}, 1'b1};  // Bit_Extender bit_extender_1
  _12_Bit_CLA u_12_bit_cla_1 (
    .A(bit_extender_1_out), .B(instruction_address), .carryIn(1'b0), .Som(n12_bit_cla_1_som));  // open: carryOut, Overflow
  _12_Bit_CLA u_12_bit_cla_2 (
    .A(branch_val), .B(instruction_address), .carryIn(1'b1), .Som(n12_bit_cla_2_som));  // open: carryOut, Overflow
  Multiplexer #(.width(12), .enable("false")) multiplexer_1 (
    .in0(n12_bit_cla_2_som), .in1(branch_val), .out(multiplexer_1_out), .sel(branch_abs));
  nor nor_1 (nor_1_out, branch_rel, branch_abs);
  Multiplexer #(.width(12), .enable("false")) multiplexer_2 (
    .in0(multiplexer_1_out), .in1(n12_bit_cla_1_som), .out(multiplexer_2_out), .sel(nor_1_out));
  register register_1 (.reset(reset), .C(C), .D(multiplexer_2_out), .Q(instruction_address));  // open: write
endmodule
